// Logisim project ALU_new.circ as structural Verilog: 1 circuit, main circuit main
module main (
  input  A,
  input  B,
  input  Selector,
  input  CarryIn,
  input  A_x,
  input  B_x,
  input  in_7,
  input  in_8,
  input  in_9,
  input  A_z,
  input  B_z,
  input  Ci_z,
  input  [1:0] Ops,
  output out_14,
  output C_out,
  output CarryOut,
  output Sum,
  output Co_z,
  output Result_z
);

  wire and_2_out, and_3_out, and_4_out, and_5_out, and_6_out, and_7_out, and_8_out, or_1_out, or_2_out,
       xor_2_out, xor_3_out;

  and and_1 (CarryOut, in_8, in_9);
  xor xor_1 (Sum, in_8, in_9);
  and and_2 (and_2_out, A_z, B_z);
  or or_1 (or_1_out, A_z, B_z);
  and and_3 (and_3_out, A, B);
  or or_2 (or_2_out, A, B);
  and and_4 (and_4_out, CarryIn, A_x);
  and and_5 (and_5_out, CarryIn, B_x);
  and and_6 (and_6_out, A_x, B_x);
  xor xor_2 (xor_2_out, A_z, B_z);
  and and_7 (and_7_out, Ci_z, xor_2_out);
  and and_8 (and_8_out, A_z, B_z);
  Multiplexer multiplexer_1 (.in0(and_3_out), .in1(or_2_out), .out(out_14), .sel(Selector));
  or or_3 (C_out, and_4_out, and_5_out, and_6_out);
  xor xor_3 (xor_3_out, xor_2_out, Ci_z);
  Multiplexer #(.select(2)) multiplexer_2 (
    .in0(xor_3_out), .in1(and_2_out), .in2(or_1_out), .in3(or_1_out), .out(Result_z), .sel(Ops));
  or or_4 (Co_z, and_7_out, and_8_out);

  // Notes on the sheet:
  //   ALU
  //   Half-Adder
  //   Logical AND OR
  //   ADDER
  //   CarryOut
  //   Full Adder
  //   ALU
endmodule
