// Logisim project alu.circ as structural Verilog: 1 circuit, main circuit main
module main (
  input  [1:0] OpSelector,
  input  Ainvert,
  input  Cin,
  input  A1,
  input  A0,
  input  B1,
  input  B0,
  input  Binvert,
  input  in_9,
  input  in_10,
  input  Aa0,
  input  Bb0,
  input  CarryIn,
  output out_14,
  output out_15,
  output out_16,
  output out_17
);

  wire adder_1_out, adder_2_out, and_1_out, and_2_out, and_3_out, and_4_out, and_5_out, and_6_out, and_7_out,
       multiplexer_1_out, multiplexer_2_out, multiplexer_3_out, multiplexer_4_out, not_1_out, not_2_out,
       not_3_out, not_4_out, Op00_out, Op01_out, or_1_out, or_2_out, or_4_out, or_5_out, undriven, undriven_2;

  Clock clock_1 ();  // open: out
  and and_1 (and_1_out, Aa0, Bb0);
  and and_2 (and_2_out, Bb0, CarryIn);
  and and_3 (and_3_out, Cin, B0);
  and and_4 (and_4_out, A0, Cin);
  or or_1 (or_1_out, and_1_out, and_2_out);
  and and_5 (and_5_out, Aa0, CarryIn);
  Multiplexer #(.enable("false")) multiplexer_1 (.in0(A0), .in1(not_1_out), .out(multiplexer_1_out), .sel(Ainvert));
  not not_1 (not_1_out, A0);
  not not_2 (not_2_out, B0);
  or or_2 (or_2_out, and_3_out, and_4_out);
  not not_3 (not_3_out, A1);
  not not_4 (not_4_out, B1);
  or or_3 (out_17, or_1_out, and_5_out);
  and Op00 (Op00_out, multiplexer_1_out, B0);
  or Op01 (Op01_out, multiplexer_1_out, B0);
  Adder #(.width(1)) adder_1 (
    .a(multiplexer_1_out), .b(multiplexer_2_out), .out(adder_1_out), .cin(Cin));  // open: cout
  Multiplexer #(.enable("false")) multiplexer_2 (.in0(B0), .in1(not_2_out), .out(multiplexer_2_out), .sel(Binvert));
  and and_6 (and_6_out, A0, B0);
  Multiplexer #(.enable("false")) multiplexer_3 (.in0(A1), .in1(not_3_out), .out(multiplexer_3_out), .sel(in_9));
  Multiplexer #(.enable("false")) multiplexer_4 (.in0(B1), .in1(not_4_out), .out(multiplexer_4_out), .sel(in_10));
  or or_4 (or_4_out, or_2_out, and_6_out);
  and and_7 (and_7_out, multiplexer_3_out, B1);
  or or_5 (or_5_out, multiplexer_3_out, B1);
  Adder #(.width(1)) adder_2 (
    .a(multiplexer_3_out), .b(multiplexer_4_out), .out(adder_2_out), .cin(or_4_out), .cout(out_16));
  Multiplexer #(.enable("false"), .select(2)) multiplexer_5 (
    .in0(Op00_out), .in1(Op01_out), .in2(adder_1_out), .in3(undriven), .out(out_15), .sel(OpSelector));
  Multiplexer #(.enable("false"), .select(2)) multiplexer_6 (
    .in0(and_7_out), .in1(or_5_out), .in2(adder_2_out), .in3(undriven_2), .out(out_14), .sel(OpSelector));

  // Notes on the sheet:
  //   ALU
  //   (NotA * B * Cin) + (A * NotB * Cin) + (A * B * NotCin) + (A * B * Cin)
endmodule
