// Logisim project alu2.circ as structural Verilog: 1 circuit, main circuit main
module main (
  input  [1:0] OpSelector,
  input  Ainvert,
  input  Cin,
  input  A2,
  input  A1,
  input  A0,
  input  B2,
  input  B1,
  input  B0,
  input  Binvert,
  input  in_11,
  input  in_12,
  input  in_13,
  input  in_14,
  output out_15,
  output out_16,
  output out_17
);

  wire adder_1_out, adder_2_cout, adder_2_out, adder_3_out, and_1_out, and_2_out, and_3_out,
       multiplexer_1_out, multiplexer_2_out, multiplexer_3_out, multiplexer_4_out, multiplexer_5_out,
       multiplexer_6_out, not_1_out, not_2_out, not_3_out, not_4_out, not_5_out, not_6_out, Op00_out,
       Op01_out, or_1_out, or_2_out, undriven, undriven_2, undriven_3, undriven_4;

  Multiplexer #(.enable("false")) multiplexer_1 (.in0(A0), .in1(not_1_out), .out(multiplexer_1_out), .sel(Ainvert));
  not not_1 (not_1_out, A0);
  not not_2 (not_2_out, B0);
  and and_1 (and_1_out, A0, B0);
  not not_3 (not_3_out, A1);
  not not_4 (not_4_out, B1);
  Multiplexer #(.enable("false")) multiplexer_2 (.in0(A2), .in1(not_5_out), .out(multiplexer_2_out), .sel(in_13));
  not not_5 (not_5_out, A2);
  Multiplexer #(.enable("false")) multiplexer_3 (.in0(B2), .in1(not_6_out), .out(multiplexer_3_out), .sel(in_14));
  not not_6 (not_6_out, B2);
  and Op00 (Op00_out, multiplexer_1_out, B0);
  or Op01 (Op01_out, multiplexer_1_out, B0);
  Adder #(.width(1)) adder_1 (
    .a(multiplexer_1_out), .b(multiplexer_4_out), .out(adder_1_out), .cin(Cin));  // open: cout
  Multiplexer #(.enable("false")) multiplexer_4 (.in0(B0), .in1(not_2_out), .out(multiplexer_4_out), .sel(Binvert));
  Multiplexer #(.enable("false")) multiplexer_5 (.in0(A1), .in1(not_3_out), .out(multiplexer_5_out), .sel(in_11));
  Multiplexer #(.enable("false")) multiplexer_6 (.in0(B1), .in1(not_4_out), .out(multiplexer_6_out), .sel(in_12));
  and and_2 (and_2_out, multiplexer_2_out, B2);
  or or_1 (or_1_out, multiplexer_2_out, B2);
  Adder #(.width(1)) adder_2 (
    .a(multiplexer_2_out), .b(multiplexer_3_out), .out(adder_2_out), .cin(undriven), .cout(adder_2_cout));
  and and_3 (and_3_out, multiplexer_5_out, B1);
  or or_2 (or_2_out, multiplexer_5_out, B1);
  Adder #(.width(1)) adder_3 (
    .a(multiplexer_5_out), .b(multiplexer_6_out), .out(adder_3_out), .cin(and_1_out));  // open: cout
  Multiplexer #(.enable("false"), .select(2)) multiplexer_7 (
    .in0(Op00_out), .in1(Op01_out), .in2(adder_1_out), .in3(undriven_3), .out(out_17), .sel(OpSelector));
  Multiplexer #(.enable("false"), .select(2)) multiplexer_8 (
    .in0(and_2_out), .in1(or_1_out), .in2(adder_2_out), .in3(undriven_2), .out(out_15), .sel(OpSelector));
  Multiplexer #(.enable("false"), .select(2)) multiplexer_9 (
    .in0(and_3_out), .in1(or_2_out), .in2(adder_3_out), .in3(undriven_4), .out(out_16), .sel(OpSelector));
endmodule
