// Logisim project encoder_decoder.circ as structural Verilog: 1 circuit, main circuit main
module main (
  input  A1,
  input  A0,
  input  x11,
  input  x10,
  input  x01,
  input  x00,
  output out_7,
  output out_8,
  output out_9,
  output out_10,
  output out_11,
  output out_12
);

  wire not_1_out, not_2_out;

  not not_1 (not_1_out, A1);
  not not_2 (not_2_out, A0);
  and o00 (out_7, not_1_out, not_2_out);
  and o01 (out_8, not_1_out, A0);
  and o10 (out_9, A1, not_2_out);
  and o11 (out_10, A1, A0);
  or or_1 (out_11, x11, x10);
  or or_2 (out_12, x11, x01);

  // Notes on the sheet:
  //   2-4 Decoder
  //   4-2 Encoder
endmodule
