// Logisim project eq2.circ as structural Verilog: 1 circuit, main circuit main
module main (
  input  A,
  input  B,
  output out_3,
  output out_4
);

  wire and_1_out, not_1_out, not_2_out, or_1_out;

  not not_1 (not_1_out, A);
  or or_1 (or_1_out, not_1_out, B);
  not not_2 (not_2_out, or_1_out);
  and and_1 (and_1_out, not_2_out, A);
  or or_2 (out_4, not_1_out, B);
  not not_3 (out_3, and_1_out);

  // Notes on the sheet:
  //   !(!(!A + B) * A) => !A + B
endmodule
