// Logisim project eq3.circ as structural Verilog: 1 circuit, main circuit main
module main (
  input  A,
  input  B,
  output out_3,
  output out_4
);

  wire and_1_out, and_2_out, not_1_out, not_2_out, not_4_out, or_1_out, or_2_out;

  not not_1 (not_1_out, A);
  not not_2 (not_2_out, B);
  not not_3 (out_4, A);
  and and_1 (and_1_out, A, B);
  or or_1 (or_1_out, not_1_out, B);
  or or_2 (or_2_out, not_2_out, B);
  not not_4 (not_4_out, and_1_out);
  and and_2 (and_2_out, not_4_out, or_1_out);
  and and_3 (out_3, and_2_out, or_2_out);
endmodule
