// Logisim project eq4.circ as structural Verilog: 1 circuit, main circuit main
module main (
  input  A,
  input  B,
  output out_3,
  output out_4
);

  wire and_1_out;

  and and_1 (and_1_out, A, B);
  or or_1 (out_3, A, and_1_out);

  assign out_4 = A;
endmodule
