// Logisim project eq_1.circ as structural Verilog: 1 circuit, main circuit main
module main (
  input  A,
  input  B,
  output out_3,
  output out_4
);

  wire not_1_out, not_2_out, not_3_out, or_1_out;

  not not_1 (not_1_out, A);
  not not_2 (not_2_out, B);
  or or_1 (or_1_out, not_1_out, not_2_out);
  not not_3 (not_3_out, or_1_out);
  and and_1 (out_3, A, not_3_out);
  and and_2 (out_4, A, B);

  // Notes on the sheet:
  //   A * !(!A + !B) = A * B 
endmodule
