// Logisim project fulladder.circ as structural Verilog: 1 circuit, main circuit main
module main (
  input  R,
  input  S,
  input  A,
  input  B,
  input  C,
  output Q,
  output Q_Inversed,
  output Cout1,
  output Sum1
);

  wire and_1_out, and_2_out, xor_1_out;

  nor nor_1 (Q, R, Q_Inversed);
  nor nor_2 (Q_Inversed, Q, S);
  xor xor_1 (xor_1_out, A, B);
  and and_1 (and_1_out, A, B);
  or or_1 (Cout1, and_2_out, and_1_out);
  xor xor_2 (Sum1, xor_1_out, C);
  and and_2 (and_2_out, xor_1_out, C);

  // Notes on the sheet:
  //   Full Adder
endmodule
