// Logisim project hw3.circ as structural Verilog: 1 circuit, main circuit main
module main (
  input  A,
  input  B,
  input  C
);

  wire not_1_out;

  not not_1 (not_1_out, A);
  LED led_1 (.in(not_1_out));
  LED led_2 (.in(A));
  // also tied to GND on the sheet: {B, C}
endmodule
