// Logisim project laws.circ as structural Verilog: 1 circuit, main circuit main
module main (
  input  A,
  input  in_2,
  input  A_a,
  input  in_4,
  input  in_5,
  input  in_6,
  input  in_7,
  input  in_8,
  input  in_9,
  input  in_10,
  input  in_11,
  input  in_12,
  input  in_13,
  input  in_14,
  input  in_15,
  input  in_16,
  input  in_17,
  input  in_18,
  input  in_19,
  input  in_20,
  input  in_21,
  input  in_22,
  input  in_23,
  input  in_24,
  input  in_25,
  input  in_26,
  output o_A,
  output o_Aa,
  output out_29,
  output out_30,
  output out_31,
  output out_32,
  output out_33,
  output out_34,
  output out_35,
  output out_36,
  output out_37,
  output out_38
);

  wire and_4_out, and_5_out, and_7_out, not_1_out, not_2_out, not_3_out, not_4_out, not_5_out, not_6_out,
       or_1_out, or_2_out, or_3_out, or_7_out;

  not not_1 (not_1_out, in_6);
  not not_2 (not_2_out, in_5);
  or or_1 (or_1_out, in_8, in_9);
  or or_2 (or_2_out, in_10, in_11);
  or or_3 (or_3_out, in_14, in_15);
  not not_3 (not_3_out, in_21);
  not not_4 (not_4_out, in_22);
  not not_5 (not_5_out, in_25);
  not not_6 (not_6_out, in_26);
  or or_4 (o_A, A, in_2);
  and and_1 (o_Aa, A_a, in_4);
  or or_5 (out_29, in_5, not_2_out);
  and and_2 (out_30, in_6, not_1_out);
  or or_6 (out_32, or_2_out, in_12);
  and and_3 (out_33, in_13, or_3_out);
  and and_4 (and_4_out, in_16, in_17);
  and and_5 (and_5_out, in_16, in_18);
  or or_7 (or_7_out, in_19, in_20);
  not not_7 (out_35, or_7_out);
  and and_6 (out_36, not_3_out, not_4_out);
  and and_7 (and_7_out, in_23, in_24);
  not not_8 (out_37, and_7_out);
  or or_8 (out_38, not_5_out, not_6_out);
  or or_9 (out_31, in_7, or_1_out);
  or or_10 (out_34, and_4_out, and_5_out);

  // Notes on the sheet:
  //   Inverse
  //   DeMorgan’s Theorems
  //   Zero and One
  //   Commutative
  //   Associative
  //   Distributive
endmodule
