// Logisim project logic_gates.circ as structural Verilog: 1 circuit, main circuit main
module main (
  input  Input_A,
  input  Input_B,
  input  Or_A,
  input  Or_B,
  input  Not_A,
  output out_6,
  output out_7,
  output out_8
);

  and and_1 (out_6, Input_A, Input_B);
  or or_1 (out_7, Or_A, Or_B);
  not not_1 (out_8, Not_A);

  // Notes on the sheet:
  //   AND
  //   OR
  //   NOT
endmodule
