// Logisim project my_plexers.circ as structural Verilog: 1 circuit, main circuit main
module main (
  input  A,
  input  B,
  input  in_3,
  output out_4
);

  wire and_1_out, and_2_out, multiplexer_1_out, not_1_out, undriven, undriven_2, undriven_3;

  Decoder decoder_1 ();  // open: out0, out1, sel, en
  Multiplexer multiplexer_1 (.in0(undriven), .in1(undriven_2), .out(multiplexer_1_out), .sel(undriven_3));
  not not_1 (not_1_out, in_3);
  and and_1 (and_1_out, A, not_1_out);
  and and_2 (and_2_out, in_3, B);
  or or_1 (out_4, and_1_out, and_2_out);
endmodule
