// Logisim project problem1.circ as structural Verilog: 1 circuit, main circuit main
module main (
  input  A,
  input  B,
  input  C,
  input  in_4,
  input  in_5,
  output Ouput_D,
  output Output_F,
  output Output_E,
  output out_9,
  output out_10,
  output out_11
);

  wire and_1_out, and_4_out, and_5_out, and_6_out, nand_1_out, or_1_out, or_2_out, or_4_out, or_5_out,
       undriven, undriven_2;

  xor xor_1 (out_10, undriven_2, undriven);
  nand nand_1 (nand_1_out, undriven_2, undriven);
  or or_1 (or_1_out, undriven, undriven_2);
  or or_2 (or_2_out, A, B);
  and and_1 (and_1_out, A, B);
  and and_2 (out_11, nand_1_out, or_1_out);
  or or_3 (Ouput_D, or_2_out, C);
  and and_3 (Output_F, and_1_out, C);
  and and_4 (and_4_out, A, B);
  and and_5 (and_5_out, A, C);
  and and_6 (and_6_out, B, C);
  and and_7 (out_9, in_4, in_5);
  or or_4 (or_4_out, and_4_out, and_5_out);
  or or_5 (or_5_out, or_4_out, and_6_out);
  xor xor_2 (Output_E, or_5_out, Output_F);
endmodule
