// Logisim project problem2.circ as structural Verilog: 1 circuit, main circuit main
module main (
  input  A,
  input  B,
  input  A_x,
  input  B_x,
  output out_5,
  output out_6
);

  wire and_1_out, and_2_out, not_1_out;

  not not_1 (not_1_out, A_x);
  and and_1 (and_1_out, not_1_out, B_x);
  and and_2 (and_2_out, A_x, B_x);
  or or_1 (out_6, and_1_out, and_2_out);

  assign out_5 = B;
  // also tied to GND on the sheet: A
endmodule
