// Logisim project problem3.circ as structural Verilog: 1 circuit, main circuit main
module main (
  input  A,
  input  B,
  input  C,
  output D_x,
  output E,
  output D
);

  wire and_1_out, and_2_out, and_3_out, and_4_out, and_5_out, and_6_out, and_7_out, and_8_out, nand_1_out,
       nor_1_out, not_1_out, not_2_out, not_3_out, or_2_out, or_3_out, undriven, undriven_2, undriven_3;

  not not_1 (not_1_out, undriven);
  and and_1 (and_1_out, not_1_out, undriven_2);
  not not_2 (not_2_out, undriven_3);
  and and_2 (and_2_out, A, B, C);
  and and_3 (and_3_out, and_1_out, not_2_out);
  and and_4 (and_4_out, and_1_out, undriven_3);
  and and_5 (and_5_out, undriven, undriven_2);
  and and_6 (and_6_out, A, C);
  // NOT_Gate not_3 has open pins: in=open, out=not_3_out
  // NAND_Gate nand_1 has open pins: out=nand_1_out
  // NOR_Gate nor_1 has open pins: out=nor_1_out
  or or_1 (E, and_6_out, and_2_out);
  or or_2 (or_2_out, and_3_out, and_4_out);
  and and_7 (and_7_out, and_5_out, not_3_out);
  and and_8 (and_8_out, undriven, undriven_2);
  or or_3 (or_3_out, or_2_out, and_7_out);
  or or_4 (D, or_3_out, and_8_out);

  assign D_x = B;
endmodule
