// Logisim project universal_gates.circ as structural Verilog: 1 circuit, main circuit main
module main (
  input  A,
  input  B,
  input  in_3,
  input  in_4,
  input  in_5,
  input  in_6,
  input  in_7,
  input  in_8,
  output out_9,
  output out_10,
  output out_11,
  output out_12
);

  wire nand_2_out, or_1_out;

  nand nand_1 (out_9, A, B);
  nor nor_1 (out_10, in_3, in_4);
  xor xor_1 (out_11, in_5, in_6);
  nand nand_2 (nand_2_out, in_7, in_8);
  or or_1 (or_1_out, in_8, in_7);
  and and_1 (out_12, nand_2_out, or_1_out);
endmodule
